# Fritzing sketch TL431_Test (saved by Fritzing 0.9.2b)
breadboards: 1

parts:
  U1 = mystery part, 3 pins [chip_label=TL431]
  R1 = Resistor [tolerance=±5% resistance=1k package=THT]

nets:
  N1: U1.pin1, U1.pin3, R1.Pin_0

notes:
  TL431
  REF
  ANODE
  CATHODE
  GND
  +5V
  Vout
