# Fritzing sketch Thermistor_103AT_PrototypingKit_Test (saved by Fritzing 0.9.2b)
breadboards: 2
perfboards: 1

parts:
  U1 = mystery part, 3 pins [chip_label=TL431]
  R1 = Resistor [tolerance=±5% resistance=1k package=THT]
  R3 = Resistor [tolerance=±5% resistance=10k package=THT]
  R4 = Temperature Sensor (Thermistor) [thermistor_type=NTC package=THT]
  LCD1 = LCD screen
  R5 = Resistor [tolerance=±5% resistance=1k package=THT]
  R6 = TRIMPOT [package=3362u-2]
  J1 = female pin header, 22 pins [form="♀ (female)"]
  J2 = female pin header, 22 pins [form="♀ (female)"]
  J3 = female pin header, 7 pins [form="♀ (female)"]  # not connected
  J4 = female pin header, 7 pins [form="♀ (female)"]  # not connected

nets:
  N1: U1.pin1, U1.pin3, R1.Pin_0, J2.pin13
  N2: U1.pin2, R3.Pin_1, J1.pin2, J1.pin18
  N3: R1.Pin_1, J1.pin1
  N4: R3.Pin_0, R4.pin_1, J1.pin19, J1.pin20
  N5: R4.pin_0, J1.pin21, J2.pin15, J2.pin20
  N6: LCD1.VSS, LCD1.LED-, R6.CW
  N7: LCD1.VDD, R5.Pin_0, R6.CCW, J2.pin21, J2.pin22
  N8: LCD1.V0, R6.WIPER
  N9: LCD1.RS, J2.pin10
  N10: LCD1.R/W, J2.pin11
  N11: LCD1.E, J2.pin9
  N12: LCD1.DB4, J2.pin5
  N13: LCD1.DB5, J2.pin6
  N14: LCD1.DB6, J2.pin7
  N15: LCD1.DB7, J2.pin8
  N16: LCD1.LED+, R5.Pin_1

notes:
  TL431
  REF
  ANODE
  CATHODE
  GND
  +5V
  V_therm
  V_hi
  PSoC 4 Prototyping Kit
  ADC
  Vref
