# Fritzing sketch Thermistor_103AT_Test (saved by Fritzing 0.9.2b)
breadboards: 2
perfboards: 1

parts:
  U1 = mystery part, 3 pins [chip_label=TL431]
  R1 = Resistor [tolerance=±5% resistance=1k package=THT]
  R3 = Resistor [tolerance=±5% resistance=10k package=THT]
  R4 = Temperature Sensor (Thermistor) [thermistor_type=NTC package=THT]
  J1 = single row smd female pin header, 9 pins [form="♀ (female)"]  # not connected
  J2 = single row smd female pin header, 9 pins [form="♀ (female)"]
  J3 = female pin header, 8 pins [form="♀ (female)"]  # not connected
  J4 = female pin header, 8 pins [form="♀ (female)"]
  J5 = female pin header, 10 pins [form="♀ (female)"]
  J6 = female pin header, 6 pins [form="♀ (female)"]
  J7 = female pin header, 6 pins [form="♀ (female)"]
  LCD1 = LCD screen
  R5 = Resistor [tolerance=±5% resistance=1k package=THT]
  R6 = TRIMPOT [package=3362u-2]

nets:
  N1: U1.pin1, U1.pin3, R1.Pin_0
  N2: U1.pin2, R3.Pin_1, LCD1.VSS, LCD1.LED-, R6.CW
  N3: R1.Pin_1, LCD1.VDD, R5.Pin_0, R6.CCW
  N4: R3.Pin_0, R4.pin_1
  N5: R4.pin_0, J2.pin2, J5.pin8
  N6: J4.pin1, LCD1.E
  N7: J4.pin2, LCD1.RS
  N8: J5.pin6, LCD1.R/W
  N9: J5.pin9, J6.pin5
  N10: J5.pin10, J7.pin5
  N11: LCD1.V0, R6.WIPER
  N12: LCD1.LED+, R5.Pin_1

notes:
  TL431
  REF
  ANODE
  CATHODE
  GND
  +5V
  V_therm
  V_hi
  PSoC 4 Pioneer Kit
  ADC
  Vref
